// Logisim project sap1_auto_avishek.circ as structural Verilog: 13 circuits, main circuit main
module main (
  input  in_1,
  input  in_2,
  input  in_3,
  output [3:0] out_4,
  output [7:0] out_5,
  output [7:0] out_6,
  output [7:0] out_7,
  output [7:0] out_8,
  output [7:0] out_9,
  output [7:0] out_10,
  output [7:0] out_11,
  output [7:0] out_12,
  output [7:0] out_13,
  output [7:0] out_14,
  output [7:0] out_15,
  output [7:0] out_16,
  output [7:0] out_17,
  output [7:0] out_18,
  output [7:0] out_19,
  output [7:0] out_20,
  output [7:0] out_21,
  output [7:0] out_22,
  output [7:0] out_23,
  output [3:0] out_24,
  output [3:0] out_25,
  output [3:0] out_26
);

  wire a_in, a_out, alu_out, alu_sub, b_in, b_out, hlt, ins_reg_in_en, ins_reg_out_en, jmp_en, l1, l2,
       mar_in_en, pc_en, pc_out, sram_rd, sram_wr;
  wire [3:0] multiplexer_1_out, multiplexer_1_out_2;
  wire [7:0] debug_data;
  wire [7:4] undriven;

  Hex_Digit_Display hex_digit_display_1 (.value(multiplexer_1_out_2));  // open: dp
  Hex_Digit_Display hex_digit_display_2 (.value(multiplexer_1_out));  // open: dp
  Multiplexer #(.width(8)) multiplexer_1 (
    .in0(out_6), .in1({undriven, out_26}), .out({multiplexer_1_out_2, multiplexer_1_out}), .sel(in_1));
  pc_with_loader pc_with_loader_1 (
    .pc_reset(in_2), .load_or_count(jmp_en), .pc_en(pc_en), .clk(in_3), .data_load(out_6[3:0]),
    .pc_out_en(pc_out), .pc_value(out_4), .pc_out(out_6[3:0]));
  Hex_Digit_Display hex_digit_display_3 (.value(out_4));  // open: dp
  Hex_Digit_Display hex_digit_display_4 (.value(out_6[7:4]));  // open: dp
  sram sram_1 (
    .sram_rd(sram_rd), .sram_wr(sram_wr), .sram_d_in(out_6),
    .mar_d_in({multiplexer_1_out_2, multiplexer_1_out}), .mar_in_en(mar_in_en), .sram_clk(in_3),
    .sram_d_out(out_6), .out_8(out_7), .out_9(out_8), .out_10(out_9), .out_11(out_10), .out_12(out_11),
    .out_13(out_12), .out_14(out_14), .out_15(out_15), .out_16(out_16), .out_17(out_17), .out_18(out_18),
    .out_19(out_19), .out_20(out_20), .out_21(out_21), .out_22(out_22), .out_23(out_23));
  Hex_Digit_Display hex_digit_display_5 (.value(out_26));  // open: dp
  ins_loader ins_loader_1 (
    .bc_reset(in_2), .bc_en(l2), .clk(in_3), .debug(in_1), .bc_address(out_26), .l1(l1), .l2(l2));
  Hex_Digit_Display hex_digit_display_6 (.value(out_6[3:0]));  // open: dp
  ROM #(.addrWidth(4)) rom_1 (.addr(out_26), .data(debug_data));
  assign out_6 = in_1 ? debug_data : 8'bz;  // Controlled_Buffer controlled_buffer_1
  Hex_Digit_Display hex_digit_display_7 (.value(out_6[3:0]));  // open: dp
  reg_gp reg_gp_1 (
    .reg_in(out_6), .reg_in_en(a_in), .reg_clk(in_3), .reg_out_en(a_out), .reg_int_out(out_5), .reg_out(out_6));
  reg_gp reg_gp_2 (
    .reg_in(out_6), .reg_in_en(b_in), .reg_clk(in_3), .reg_out_en(b_out), .reg_int_out(out_13),
    .reg_out(out_6));
  Hex_Digit_Display hex_digit_display_8 (.value(out_25));  // open: dp
  ins_reg ins_reg_1 (
    .ins_reg_in(out_6), .ins_reg_in_en(ins_reg_in_en), .clk(in_3), .ins_reg_out_en(ins_reg_out_en),
    .add_outs(out_6[3:0]), .ins_out(out_25));
  Hex_Digit_Display hex_digit_display_9 (.value(out_5[7:4]));  // open: dp
  Hex_Digit_Display hex_digit_display_10 (.value(out_5[3:0]));  // open: dp
  alu alu_1 (
    .alu_in_1(out_5), .alu_out_en(alu_out), .alu_sub(alu_sub), .alu_in_2(out_13), .alu_out(out_6));  // open: alu_carry_out
  Hex_Digit_Display hex_digit_display_11 (.value(out_13[7:4]));  // open: dp
  Hex_Digit_Display hex_digit_display_12 (.value(out_13[3:0]));  // open: dp
  LED led_1 (.in(in_1));
  control_sequence control_sequence_1 (
    .clk(in_3), .clk_reset(in_2), .ins_msb(out_25), .l1(l1), .debug(in_1), .l2(l2), .pc_en(pc_en),
    .pc_out_final(pc_out), .a_in(a_in), .jmp_en(jmp_en), .a_out_final(a_out), .alu_out(alu_out),
    .mar_in_en_final(mar_in_en), .sram_rd_final(sram_rd), .sram_wr_final(sram_wr), .hlt(hlt),
    .sub_out(alu_sub), .ins_reg_in_en(ins_reg_in_en), .ins_reg_out_en(ins_reg_out_en), .b_in(b_in));

  assign out_24 = out_6[3:0];

  // Other names for the same wires on the sheet: bc_address[3:0] = out_26; clk = in_3; debug = in_1;
  //   ir_operand[3:0] = out_6[3:0]; pc_reset = in_2

  // Notes on the sheet:
  //   MAR Value
  //   Counter Value
  //   Data Bus
  //   Loader Counter Value
  //   contents of rom_1 (hex, n*v repeats v):
  //   1d 2e 65 0 0 30 5f f0 5*0 33 19
  //   Instruction Operand
  //   Instruction Opcode
  //   REG A
  //   REG B
  //   Code Loading Mode LED
  //   Clock & Reset
  //   Code Loading Pin
endmodule

module reg_gp (
  input  [7:0] reg_in,
  input  reg_in_en,
  input  reg_clk,
  input  reg_out_en,
  output [7:0] reg_int_out,
  output [7:0] reg_out
);

  wire multiplexer_1_out, multiplexer_2_out, multiplexer_3_out, multiplexer_4_out, multiplexer_5_out,
       multiplexer_6_out, multiplexer_7_out, multiplexer_8_out;

  Multiplexer multiplexer_1 (.in0(reg_int_out[7]), .in1(reg_in[7]), .out(multiplexer_1_out), .sel(reg_in_en));
  D_Flip_Flop d_ff_1 (.D(multiplexer_1_out), .clk(reg_clk), .Q(reg_int_out[7]));  // open: Qn, preset, reset
  assign reg_out[7] = reg_out_en ? reg_int_out[7] : 1'bz;  // Controlled_Buffer controlled_buffer_1
  Multiplexer multiplexer_2 (.in0(reg_int_out[6]), .in1(reg_in[6]), .out(multiplexer_2_out), .sel(reg_in_en));
  D_Flip_Flop d_ff_2 (.D(multiplexer_2_out), .clk(reg_clk), .Q(reg_int_out[6]));  // open: Qn, preset, reset
  Multiplexer multiplexer_3 (.in0(reg_int_out[5]), .in1(reg_in[5]), .out(multiplexer_3_out), .sel(reg_in_en));
  assign reg_out[6] = reg_out_en ? reg_int_out[6] : 1'bz;  // Controlled_Buffer controlled_buffer_2
  D_Flip_Flop d_ff_3 (.D(multiplexer_3_out), .clk(reg_clk), .Q(reg_int_out[5]));  // open: Qn, preset, reset
  Multiplexer multiplexer_4 (.in0(reg_int_out[4]), .in1(reg_in[4]), .out(multiplexer_4_out), .sel(reg_in_en));
  assign reg_out[5] = reg_out_en ? reg_int_out[5] : 1'bz;  // Controlled_Buffer controlled_buffer_3
  D_Flip_Flop d_ff_4 (.D(multiplexer_4_out), .clk(reg_clk), .Q(reg_int_out[4]));  // open: Qn, preset, reset
  Multiplexer multiplexer_5 (.in0(reg_int_out[3]), .in1(reg_in[3]), .out(multiplexer_5_out), .sel(reg_in_en));
  assign reg_out[4] = reg_out_en ? reg_int_out[4] : 1'bz;  // Controlled_Buffer controlled_buffer_4
  D_Flip_Flop d_ff_5 (.D(multiplexer_5_out), .clk(reg_clk), .Q(reg_int_out[3]));  // open: Qn, preset, reset
  Multiplexer multiplexer_6 (.in0(reg_int_out[2]), .in1(reg_in[2]), .out(multiplexer_6_out), .sel(reg_in_en));
  D_Flip_Flop d_ff_6 (.D(multiplexer_6_out), .clk(reg_clk), .Q(reg_int_out[2]));  // open: Qn, preset, reset
  assign reg_out[3] = reg_out_en ? reg_int_out[3] : 1'bz;  // Controlled_Buffer controlled_buffer_5
  assign reg_out[2] = reg_out_en ? reg_int_out[2] : 1'bz;  // Controlled_Buffer controlled_buffer_6
  Multiplexer multiplexer_7 (.in0(reg_int_out[1]), .in1(reg_in[1]), .out(multiplexer_7_out), .sel(reg_in_en));
  D_Flip_Flop d_ff_7 (.D(multiplexer_7_out), .clk(reg_clk), .Q(reg_int_out[1]));  // open: Qn, preset, reset
  assign reg_out[1] = reg_out_en ? reg_int_out[1] : 1'bz;  // Controlled_Buffer controlled_buffer_7
  Multiplexer multiplexer_8 (.in0(reg_int_out[0]), .in1(reg_in[0]), .out(multiplexer_8_out), .sel(reg_in_en));
  D_Flip_Flop d_ff_8 (.D(multiplexer_8_out), .clk(reg_clk), .Q(reg_int_out[0]));  // open: Qn, preset, reset
  assign reg_out[0] = reg_out_en ? reg_int_out[0] : 1'bz;  // Controlled_Buffer controlled_buffer_8

  // Notes on the sheet:
  //   Input
  //   Input Control
  //   Clock
  //   Output Control
  //   Memory
  //   Internal Output
  //   Output
endmodule

module alu (
  input  [7:0] alu_in_1,
  input  alu_out_en,
  input  alu_sub,
  input  [7:0] alu_in_2,
  output alu_carry_out,
  output [7:0] alu_out
);

  wire adder_2_cout, adder_3_cout, adder_4_cout, adder_5_cout, adder_6_cout, adder_7_cout, adder_8_cout,
       xor_1_out, xor_2_out, xor_3_out, xor_4_out, xor_5_out, xor_6_out, xor_7_out, xor_8_out;
  wire [7:0] adder_8_out;

  Adder #(.width(1)) adder_1 (
    .a(alu_in_1[7]), .b(xor_1_out), .out(adder_8_out[7]), .cin(adder_2_cout), .cout(alu_carry_out));
  xor xor_1 (xor_1_out, alu_in_2[7], alu_sub);
  Adder #(.width(1)) adder_2 (
    .a(alu_in_1[6]), .b(xor_2_out), .out(adder_8_out[6]), .cin(adder_3_cout), .cout(adder_2_cout));
  xor xor_2 (xor_2_out, alu_in_2[6], alu_sub);
  Adder #(.width(1)) adder_3 (
    .a(alu_in_1[5]), .b(xor_3_out), .out(adder_8_out[5]), .cin(adder_4_cout), .cout(adder_3_cout));
  xor xor_3 (xor_3_out, alu_in_2[5], alu_sub);
  Adder #(.width(1)) adder_4 (
    .a(alu_in_1[4]), .b(xor_4_out), .out(adder_8_out[4]), .cin(adder_5_cout), .cout(adder_4_cout));
  xor xor_4 (xor_4_out, alu_in_2[4], alu_sub);
  Adder #(.width(1)) adder_5 (
    .a(alu_in_1[3]), .b(xor_5_out), .out(adder_8_out[3]), .cin(adder_6_cout), .cout(adder_5_cout));
  xor xor_5 (xor_5_out, alu_in_2[3], alu_sub);
  Adder #(.width(1)) adder_6 (
    .a(alu_in_1[2]), .b(xor_6_out), .out(adder_8_out[2]), .cin(adder_7_cout), .cout(adder_6_cout));
  xor xor_6 (xor_6_out, alu_in_2[2], alu_sub);
  Adder #(.width(1)) adder_7 (
    .a(alu_in_1[1]), .b(xor_7_out), .out(adder_8_out[1]), .cin(adder_8_cout), .cout(adder_7_cout));
  xor xor_7 (xor_7_out, alu_in_2[1], alu_sub);
  Adder #(.width(1)) adder_8 (.a(alu_in_1[0]), .b(xor_8_out), .out(adder_8_out[0]), .cin(alu_sub), .cout(adder_8_cout));
  xor xor_8 (xor_8_out, alu_in_2[0], alu_sub);
  assign alu_out = alu_out_en ? adder_8_out : 8'bz;  // Controlled_Buffer controlled_buffer_1

  // Notes on the sheet:
  //   Input 1
  //   Carry Output
  //   Subtract Control
  //   Full Adders
  //   Input 2
  //   Output Control
  //   ALU Output
endmodule

module pc (
  input  pc_en,
  input  pc_clk,
  input  pc_reset,
  input  pc_out_en,
  output [3:0] pc_value,
  output [3:0] pc_out
);

  wire j_k_ff_2_qn, j_k_ff_3_qn, j_k_ff_4_qn;

  J_K_Flip_Flop j_k_ff_1 (
    .J(pc_en), .K(pc_en), .clk(j_k_ff_2_qn), .Q(pc_value[3]), .reset(pc_reset));  // open: Qn, preset
  J_K_Flip_Flop j_k_ff_2 (
    .J(pc_en), .K(pc_en), .clk(j_k_ff_3_qn), .Q(pc_value[2]), .Qn(j_k_ff_2_qn), .reset(pc_reset));  // open: preset
  J_K_Flip_Flop j_k_ff_3 (
    .J(pc_en), .K(pc_en), .clk(j_k_ff_4_qn), .Q(pc_value[1]), .Qn(j_k_ff_3_qn), .reset(pc_reset));  // open: preset
  J_K_Flip_Flop j_k_ff_4 (
    .J(pc_en), .K(pc_en), .clk(pc_clk), .Q(pc_value[0]), .Qn(j_k_ff_4_qn), .reset(pc_reset));  // open: preset
  assign pc_out = pc_out_en ? pc_value : 4'bz;  // Controlled_Buffer controlled_buffer_1

  // Notes on the sheet:
  //   Clock
  //   Reset
  //   Output Control
  //   Count Control
  //   Counter Output
endmodule

module dec_4x16 (
  input  [3:0] dec_in,
  output [15:0] dec_out
);

  wire not_1_out, not_2_out, not_3_out, not_4_out;

  not not_1 (not_1_out, dec_in[3]);
  not not_2 (not_2_out, dec_in[2]);
  not not_3 (not_3_out, dec_in[1]);
  not not_4 (not_4_out, dec_in[0]);
  and and_1 (dec_out[0], not_4_out, not_3_out, not_2_out, not_1_out);
  and and_2 (dec_out[1], dec_in[0], not_3_out, not_2_out, not_1_out);
  and and_3 (dec_out[2], not_4_out, dec_in[1], not_2_out, not_1_out);
  and and_4 (dec_out[3], dec_in[0], dec_in[1], not_2_out, not_1_out);
  and and_5 (dec_out[4], not_4_out, not_3_out, dec_in[2], not_1_out);
  and and_6 (dec_out[5], dec_in[0], not_3_out, dec_in[2], not_1_out);
  and and_7 (dec_out[6], not_4_out, dec_in[1], dec_in[2], not_1_out);
  and and_8 (dec_out[7], dec_in[0], dec_in[1], dec_in[2], not_1_out);
  and and_9 (dec_out[8], not_4_out, not_3_out, not_2_out, dec_in[3]);
  and and_10 (dec_out[9], dec_in[0], not_3_out, not_2_out, dec_in[3]);
  and and_11 (dec_out[10], not_4_out, dec_in[1], not_2_out, dec_in[3]);
  and and_12 (dec_out[11], dec_in[0], dec_in[1], not_2_out, dec_in[3]);
  and and_13 (dec_out[12], not_4_out, not_3_out, dec_in[2], dec_in[3]);
  and and_14 (dec_out[13], dec_in[0], not_3_out, dec_in[2], dec_in[3]);
  and and_15 (dec_out[14], not_4_out, dec_in[1], dec_in[2], dec_in[3]);
  and and_16 (dec_out[15], dec_in[0], dec_in[1], dec_in[2], dec_in[3]);
endmodule

module sram_cell (
  input  [7:0] data_in,
  input  wr_en,
  input  clk,
  input  cs,
  input  rd_en,
  output [7:0] memory_content,
  output [7:0] data_out
);

  wire and_1_out, and_2_out;

  and and_1 (and_1_out, wr_en, cs);
  and and_2 (and_2_out, cs, rd_en);
  reg_gp reg_gp_1 (
    .reg_in(data_in), .reg_in_en(and_1_out), .reg_clk(clk), .reg_out_en(and_2_out),
    .reg_int_out(memory_content), .reg_out(data_out));
endmodule

module sram (
  input  sram_rd,
  input  sram_wr,
  input  [7:0] sram_d_in,
  input  [7:0] mar_d_in,
  input  mar_in_en,
  input  sram_clk,
  output [7:0] sram_d_out,
  output [7:0] out_8,
  output [7:0] out_9,
  output [7:0] out_10,
  output [7:0] out_11,
  output [7:0] out_12,
  output [7:0] out_13,
  output [7:0] out_14,
  output [7:0] out_15,
  output [7:0] out_16,
  output [7:0] out_17,
  output [7:0] out_18,
  output [7:0] out_19,
  output [7:0] out_20,
  output [7:0] out_21,
  output [7:0] out_22,
  output [7:0] out_23
);

  wire [7:0] controlled_buffer_1_out, reg_gp_1_reg_int_out;
  wire [15:0] dec_4x16_1_dec_out;

  dec_4x16 dec_4x16_1 (.dec_in(reg_gp_1_reg_int_out[3:0]), .dec_out(dec_4x16_1_dec_out));
  reg_gp reg_gp_1 (
    .reg_in(mar_d_in), .reg_in_en(mar_in_en), .reg_clk(sram_clk), .reg_int_out(reg_gp_1_reg_int_out));  // open: reg_out_en, reg_out
  assign controlled_buffer_1_out = sram_wr ? sram_d_in : 8'bz;  // Controlled_Buffer controlled_buffer_1
  sram_cell sram_cell_1 (
    .data_in(controlled_buffer_1_out), .wr_en(sram_wr), .clk(sram_clk), .cs(dec_4x16_1_dec_out[0]),
    .rd_en(sram_rd), .memory_content(out_8), .data_out(controlled_buffer_1_out));
  sram_cell sram_cell_2 (
    .data_in(controlled_buffer_1_out), .wr_en(sram_wr), .clk(sram_clk), .cs(dec_4x16_1_dec_out[1]),
    .rd_en(sram_rd), .memory_content(out_9), .data_out(controlled_buffer_1_out));
  sram_cell sram_cell_3 (
    .data_in(controlled_buffer_1_out), .wr_en(sram_wr), .clk(sram_clk), .cs(dec_4x16_1_dec_out[2]),
    .rd_en(sram_rd), .memory_content(out_10), .data_out(controlled_buffer_1_out));
  sram_cell sram_cell_4 (
    .data_in(controlled_buffer_1_out), .wr_en(sram_wr), .clk(sram_clk), .cs(dec_4x16_1_dec_out[3]),
    .rd_en(sram_rd), .memory_content(out_11), .data_out(controlled_buffer_1_out));
  sram_cell sram_cell_5 (
    .data_in(controlled_buffer_1_out), .wr_en(sram_wr), .clk(sram_clk), .cs(dec_4x16_1_dec_out[4]),
    .rd_en(sram_rd), .memory_content(out_12), .data_out(controlled_buffer_1_out));
  sram_cell sram_cell_6 (
    .data_in(controlled_buffer_1_out), .wr_en(sram_wr), .clk(sram_clk), .cs(dec_4x16_1_dec_out[5]),
    .rd_en(sram_rd), .memory_content(out_13), .data_out(controlled_buffer_1_out));
  sram_cell sram_cell_7 (
    .data_in(controlled_buffer_1_out), .wr_en(sram_wr), .clk(sram_clk), .cs(dec_4x16_1_dec_out[6]),
    .rd_en(sram_rd), .memory_content(out_14), .data_out(controlled_buffer_1_out));
  sram_cell sram_cell_8 (
    .data_in(controlled_buffer_1_out), .wr_en(sram_wr), .clk(sram_clk), .cs(dec_4x16_1_dec_out[7]),
    .rd_en(sram_rd), .memory_content(out_15), .data_out(controlled_buffer_1_out));
  sram_cell sram_cell_9 (
    .data_in(controlled_buffer_1_out), .wr_en(sram_wr), .clk(sram_clk), .cs(dec_4x16_1_dec_out[8]),
    .rd_en(sram_rd), .memory_content(out_16), .data_out(controlled_buffer_1_out));
  sram_cell sram_cell_10 (
    .data_in(controlled_buffer_1_out), .wr_en(sram_wr), .clk(sram_clk), .cs(dec_4x16_1_dec_out[9]),
    .rd_en(sram_rd), .memory_content(out_17), .data_out(controlled_buffer_1_out));
  sram_cell sram_cell_11 (
    .data_in(controlled_buffer_1_out), .wr_en(sram_wr), .clk(sram_clk), .cs(dec_4x16_1_dec_out[10]),
    .rd_en(sram_rd), .memory_content(out_18), .data_out(controlled_buffer_1_out));
  sram_cell sram_cell_12 (
    .data_in(controlled_buffer_1_out), .wr_en(sram_wr), .clk(sram_clk), .cs(dec_4x16_1_dec_out[11]),
    .rd_en(sram_rd), .memory_content(out_19), .data_out(controlled_buffer_1_out));
  sram_cell sram_cell_13 (
    .data_in(controlled_buffer_1_out), .wr_en(sram_wr), .clk(sram_clk), .cs(dec_4x16_1_dec_out[12]),
    .rd_en(sram_rd), .memory_content(out_20), .data_out(controlled_buffer_1_out));
  sram_cell sram_cell_14 (
    .data_in(controlled_buffer_1_out), .wr_en(sram_wr), .clk(sram_clk), .cs(dec_4x16_1_dec_out[13]),
    .rd_en(sram_rd), .memory_content(out_21), .data_out(controlled_buffer_1_out));
  sram_cell sram_cell_15 (
    .data_in(controlled_buffer_1_out), .wr_en(sram_wr), .clk(sram_clk), .cs(dec_4x16_1_dec_out[14]),
    .rd_en(sram_rd), .memory_content(out_22), .data_out(controlled_buffer_1_out));
  sram_cell sram_cell_16 (
    .data_in(controlled_buffer_1_out), .wr_en(sram_wr), .clk(sram_clk), .cs(dec_4x16_1_dec_out[15]),
    .rd_en(sram_rd), .memory_content(out_23), .data_out(controlled_buffer_1_out));
  assign sram_d_out = sram_rd ? controlled_buffer_1_out : 8'bz;  // Controlled_Buffer controlled_buffer_2
endmodule

module ins_reg (
  input  [7:0] ins_reg_in,
  input  ins_reg_in_en,
  input  clk,
  input  ins_reg_out_en,
  output [3:0] add_outs,
  output [3:0] ins_out
);

  wire [3:0] reg_gp_1_reg_int_out;

  reg_gp reg_gp_1 (
    .reg_in(ins_reg_in), .reg_in_en(ins_reg_in_en), .reg_clk(clk),
    .reg_int_out({ins_out, reg_gp_1_reg_int_out}));  // open: reg_out_en, reg_out
  assign add_outs = ins_reg_out_en ? reg_gp_1_reg_int_out : 4'bz;  // Controlled_Buffer controlled_buffer_1
endmodule

module ins_dec (
  input  [3:0] ir_msb,
  output isLDA,
  output isLDB,
  output isADD,
  output isSUB,
  output isSTA,
  output isJMP,
  output isHLT
);

  wire [14:0] dec_4x16_1_dec_out;

  dec_4x16 dec_4x16_1 (
    .dec_in(ir_msb),
    .dec_out({isHLT, dec_4x16_1_dec_out[14:7], isJMP, isSTA, isSUB, isADD, isLDB, isLDA, dec_4x16_1_dec_out[0]}));
endmodule

module rc (
  input  clk,
  input  ring_reset,
  output T1,
  output T2,
  output T3,
  output T4,
  output T5,
  output T6
);

  wire controlled_buffer_1_out, not_1_out;
  wire [3:0] pc_1_pc_value;
  wire [15:6] dec_4x16_1_dec_out;

  assign controlled_buffer_1_out = ring_reset ? ring_reset : 1'bz;  // Controlled_Buffer controlled_buffer_1
  not not_1 (not_1_out, ring_reset);
  assign controlled_buffer_1_out = not_1_out ? dec_4x16_1_dec_out[6] : 1'bz;  // Controlled_Buffer controlled_buffer_2
  pc pc_1 (
    .pc_en(1'b1), .pc_clk(clk), .pc_reset(controlled_buffer_1_out), .pc_out_en(1'b1), .pc_value(pc_1_pc_value));  // open: pc_out
  dec_4x16 dec_4x16_1 (.dec_in(pc_1_pc_value), .dec_out({dec_4x16_1_dec_out, T6, T5, T4, T3, T2, T1}));
endmodule

module control_sequence (
  input  clk,
  input  clk_reset,
  input  [3:0] ins_msb,
  input  l1,
  input  debug,
  input  l2,
  output pc_en,
  output pc_out_final,
  output a_in,
  output jmp_en,
  output a_out_final,
  output alu_out,
  output mar_in_en_final,
  output sram_rd_final,
  output sram_wr_final,
  output hlt,
  output sub_out,
  output ins_reg_in_en,
  output ins_reg_out_en,
  output b_in
);

  wire and_1_out, and_4_out, and_5_out, and_6_out, and_7_out, and_8_out, and_10_out, and_12_out, and_13_out,
       and_15_out, and_16_out, and_17_out, and_18_out, and_19_out, and_21_out, and_23_out, and_25_out,
       and_27_out, and_28_out, and_29_out, and_30_out, and_32_out, ins_dec_1_isadd, ins_dec_1_ishlt,
       ins_dec_1_isjmp, ins_dec_1_islda, ins_dec_1_isldb, ins_dec_1_issta, ins_dec_1_issub, not_1_out,
       not_2_out, not_3_out, or_1_out, or_3_out, or_4_out, or_5_out, or_6_out, rc_1_t1, rc_1_t2, rc_1_t4,
       rc_1_t5;

  not not_1 (not_1_out, debug);
  not not_2 (not_2_out, debug);
  not not_3 (not_3_out, l2);
  rc rc_1 (
    .clk(clk), .ring_reset(clk_reset), .T1(rc_1_t1), .T2(rc_1_t2), .T3(pc_en), .T4(rc_1_t4), .T5(rc_1_t5));  // open: T6
  ins_dec ins_dec_1 (
    .ir_msb(ins_msb), .isLDA(ins_dec_1_islda), .isLDB(ins_dec_1_isldb), .isADD(ins_dec_1_isadd),
    .isSUB(ins_dec_1_issub), .isSTA(ins_dec_1_issta), .isJMP(ins_dec_1_isjmp), .isHLT(ins_dec_1_ishlt));
  and and_1 (and_1_out, ins_dec_1_isjmp, pc_en);
  and and_2 (jmp_en, not_3_out, and_1_out, not_2_out);
  and and_3 (pc_out_final, not_2_out, not_3_out, rc_1_t1);
  or or_1 (or_1_out, rc_1_t1, and_5_out, and_6_out, and_7_out);
  and and_4 (and_4_out, not_1_out, or_1_out);
  and and_5 (and_5_out, ins_dec_1_islda, rc_1_t4);
  and and_6 (and_6_out, ins_dec_1_isldb, rc_1_t4);
  or or_2 (mar_in_en_final, and_4_out, l1);
  and and_7 (and_7_out, ins_dec_1_issta, rc_1_t4);
  and and_8 (and_8_out, rc_1_t5, ins_dec_1_islda);
  or or_3 (or_3_out, rc_1_t2, and_8_out, and_10_out);
  and and_9 (sram_rd_final, not_2_out, not_3_out, or_3_out);
  and and_10 (and_10_out, rc_1_t5, ins_dec_1_isldb);
  and and_11 (ins_reg_in_en, not_2_out, not_3_out, rc_1_t2);
  and and_12 (and_12_out, rc_1_t4, ins_dec_1_islda);
  and and_13 (and_13_out, rc_1_t4, ins_dec_1_isldb);
  or or_4 (or_4_out, and_12_out, and_13_out, and_15_out, and_16_out);
  and and_14 (ins_reg_out_en, not_2_out, not_3_out, or_4_out);
  and and_15 (and_15_out, rc_1_t4, ins_dec_1_issta);
  and and_16 (and_16_out, pc_en, ins_dec_1_isjmp);
  and and_17 (and_17_out, ins_dec_1_issub, rc_1_t4);
  and and_18 (and_18_out, rc_1_t5, ins_dec_1_islda);
  and and_19 (and_19_out, rc_1_t4, ins_dec_1_isadd);
  or or_5 (or_5_out, and_17_out, and_18_out, and_19_out);
  and and_20 (a_in, not_2_out, not_3_out, or_5_out);
  and and_21 (and_21_out, rc_1_t5, ins_dec_1_issta);
  and and_22 (a_out_final, not_2_out, not_3_out, and_21_out);
  and and_23 (and_23_out, rc_1_t5, ins_dec_1_isldb);
  and and_24 (b_in, not_2_out, not_3_out, and_23_out);
  and and_25 (and_25_out, ins_dec_1_issub, rc_1_t4);
  or or_6 (or_6_out, and_25_out, and_27_out);
  and and_26 (alu_out, not_2_out, not_3_out, or_6_out);
  and and_27 (and_27_out, rc_1_t4, ins_dec_1_isadd);
  and and_28 (and_28_out, not_3_out, and_29_out);
  or or_7 (sram_wr_final, l2, and_28_out);
  and and_29 (and_29_out, rc_1_t5, ins_dec_1_issta);
  and and_30 (and_30_out, ins_dec_1_ishlt, rc_1_t4);
  and and_31 (hlt, not_2_out, not_3_out, and_30_out);
  and and_32 (and_32_out, ins_dec_1_issub, rc_1_t4);
  and and_33 (sub_out, not_3_out, not_2_out, and_32_out);
endmodule

module ins_loader (
  input  bc_reset,
  input  bc_en,
  input  clk,
  input  debug,
  output [3:0] bc_address,
  output l1,
  output l2
);

  wire controlled_buffer_1_out, d_ff_1_q, not_1_out;

  Counter #(.max('hf), .width(4)) counter_1 (
    .clr(bc_reset), .load(1'b0), .up(1'b1), .count(bc_en), .clk(clk), .Q(bc_address));  // open: D, carry
  D_Flip_Flop d_ff_1 (.D(controlled_buffer_1_out), .clk(clk), .Q(d_ff_1_q));  // open: Qn, preset, reset
  assign controlled_buffer_1_out = debug ? not_1_out : 1'bz;  // Controlled_Buffer controlled_buffer_1
  not not_1 (not_1_out, d_ff_1_q);
  and and_1 (l1, debug, not_1_out);
  and and_2 (l2, debug, d_ff_1_q);
endmodule

module pc_with_loader (
  input  pc_reset,
  input  load_or_count,
  input  pc_en,
  input  clk,
  input  [3:0] data_load,
  input  pc_out_en,
  output [3:0] pc_value,
  output [3:0] pc_out
);

  Counter #(.max('hf), .width(4)) counter_1 (
    .clr(pc_reset), .load(load_or_count), .up(1'b1), .count(pc_en), .clk(clk), .D(data_load), .Q(pc_value));  // open: carry
  assign pc_out = pc_out_en ? pc_value : 4'bz;  // Controlled_Buffer controlled_buffer_1
endmodule
